# Fritzing sketch Placarduino (saved by Fritzing 0.9.2b)
breadboards: 1

parts:
  Componente1 = Arduino Uno (Rev3) - ICSP
  S1 = Pushbutton [package="[THT]"]
  S2 = Pushbutton [package="[THT]"]
  R3 = Resistor [tolerance=±5% resistance=10k package=THT]
  R4 = Resistor [tolerance=±5% resistance=10k package=THT]
  Piezo2 = Piezo Speaker
  R5 = Resistor [tolerance=±5% resistance=220 package=THT]
  LCM1602_IIC1 = LCM1602 IIC [part_number="LCM1602 IIC" chip_label="LCM1602 IIC" package="DIP (Dual Inline) [THT]"]
  LCD1 = LCD screen

nets:
  N1: Componente1.A4/SDA, LCM1602_IIC1.SDA
  N2: Componente1.A5/SCL, LCM1602_IIC1.SCL
  N3: Componente1.D5_PWM, R5.Pin_0
  N4: Componente1.D6_PWM, S2.Pin_1, S2.Pin_2, R4.Pin_1
  N5: Componente1.D7, S1.Pin_1, S1.Pin_2, R3.Pin_1
  5V: Componente1.5V, S1.Pin_3, S1.Pin_4, S2.Pin_3, S2.Pin_4, LCM1602_IIC1.VCC
  GND: Componente1.GND, R3.Pin_0, R4.Pin_0, Piezo2.GND, LCM1602_IIC1.GND
  N6: Piezo2.VCC, R5.Pin_1
  VSS: LCM1602_IIC1.VSS, LCD1.VSS
  VDD: LCM1602_IIC1.VDD, LCD1.VDD
  N7: LCM1602_IIC1.V0, LCD1.V0
  N8: LCM1602_IIC1.RS, LCD1.RS
  N9: LCM1602_IIC1.RW, LCD1.R/W
  N10: LCM1602_IIC1.E, LCD1.E
  N11: LCM1602_IIC1.D0, LCD1.DB0
  N12: LCM1602_IIC1.D1, LCD1.DB1
  N13: LCM1602_IIC1.D2, LCD1.DB2
  N14: LCM1602_IIC1.D3, LCD1.DB3
  N15: LCM1602_IIC1.D4, LCD1.DB4
  N16: LCM1602_IIC1.D5, LCD1.DB5
  N17: LCM1602_IIC1.D6, LCD1.DB6
  N18: LCM1602_IIC1.D7, LCD1.DB7
  N19: LCM1602_IIC1.A, LCD1.LED+
  N20: LCM1602_IIC1.K, LCD1.LED-
  N21: LCM1602_IIC1.LED_A, LCM1602_IIC1.LED_B

notes:
  Geralmente o controlador é soldado atrás do display, mas não existe um componente assim no Fritzing.
  O Fritzing também não tem um display 20x4, mas os pinos são os mesmos do 16x2

custom parts:
  Piezo Speaker: This is a small 12mm round speaker that operates around the audible 2kHz range. You can use these speakers to create simple music or user interfaces.
  LCM1602 IIC: I2C-Module to use a 1602 or 2004 LCD on with the wire.h libory Serial LCD Modul
